# Fritzing sketch ballotbox1 (saved by Fritzing 0.9.2b)
breadboards: 1

parts:
  Controller = Arduino Uno (Rev3)
  6V_Linear_Regulator = Voltage Regulator [package=to220-adj]
  DC_Adapter = DC Power [voltage=12V]
  part = Trimmer Potentiometer [maximum_resistance=5kΩ package=THT]
  Reject_Diverter = Basic Servo [part_number=6001HB]
  IC1 = L293D [package=THT]
  Feed_Motor = DC Motor
  D1 = Diode [package=diode-1n4001]
  D2 = Diode [package=diode-1n4001]
  D3 = Diode [package=diode-1n4001]
  D4 = Diode [package=diode-1n4001]
  Reject_Mode = Pushbutton [package=THT]
  Feed_Sensor = PHOTOTRANSISTOR REFLECTIVE OBJECT SENSOR [part_number=HY301-21 package=qrb1114-side]
  R2 = Resistor [tolerance=±5% resistance=220 package=THT]
  LED1 = LED - 5mm [color="Red (633nm)" package="5 mm [THT]"]
  R3 = Resistor [tolerance=±5% resistance=220 package=THT]
  Feed_Sensor_2 = PHOTOTRANSISTOR REFLECTIVE OBJECT SENSOR [part_number=HY301-21 package=qrb1114-side]
  R4 = Resistor [tolerance=±5% resistance=220 package=THT]
  LED2 = LED - 5mm [color="Red (633nm)" package="5 mm [THT]"]
  R5 = Resistor [tolerance=±5% resistance=220 package=THT]
  Sound_Controller = Arduino Uno (Rev3)
  PC_speaker = SPEAKER [package=pcb_mount_speaker]
  Experimenter_Button = Pushbutton [package=THT]

nets:
  N1: Controller.A2, Feed_Sensor.C, R3.Pin_1
  N2: Controller.A3, Feed_Sensor_2.C, R5.Pin_1
  N3: Controller.D8, IC1.In_1
  N4: Controller.D9_PWM, Reject_Diverter.pulse
  N5: Controller.D10_PWM/SS, Sound_Controller.D10_PWM/SS
  N6: Controller.D11_PWM/MOSI, Sound_Controller.D11_PWM/MOSI
  N7: Controller.D12/MISO, Sound_Controller.D12/MISO
  GND: Controller.GND, DC_Adapter.V-, part.leg1, Reject_Diverter.gnd, IC1.0V, D3.A, D4.A, Reject_Mode.leg0, Feed_Sensor.K, LED1.cathode, Feed_Sensor_2.K, LED2.cathode, Sound_Controller.GND, PC_speaker.-, Experimenter_Button.leg0
  N8: Controller.D3_PWM, Experimenter_Button.leg1
  N9: Controller.D4, Reject_Mode.leg1
  N10: Controller.D6_PWM, IC1.In_2
  N11: Controller.D7, IC1.Enable_1
  N12: Controller.5V, IC1.+Vmotor, IC1.+V, D1.C, D2.C, R2.Pin_0, R3.Pin_0, R4.Pin_0, R5.Pin_0
  VIN: Controller.VIN, 6V_Linear_Regulator.IN, DC_Adapter.V+, Sound_Controller.VIN
  N13: 6V_Linear_Regulator.ADJ, part.leg2
  N14: 6V_Linear_Regulator.OUT, part.wiper, Reject_Diverter.vcc
  N15: IC1.Out_1_(_Controlled_by_Enable_1_), Feed_Motor.pin_1, D1.A, D4.C
  N16: IC1.Out_2_(_Controlled_by_Enable_1_), Feed_Motor.pin_2, D2.A, D3.C
  N17: Feed_Sensor.A, R2.Pin_1
  N18: Feed_Sensor.E, LED1.anode
  N19: Feed_Sensor_2.A, R4.Pin_1
  N20: Feed_Sensor_2.E, LED2.anode
  N21: Sound_Controller.D8, PC_speaker.+
